// Digital circuit q-clock-v2.dig as structural Verilog
module q_clock_v2 (
  input  Scan,
  input  Clock,
  output Inverted,
  output Primary
);

  wire Auto_out, d_ff_1_q, d_ff_2_q, d_ff_3_nq, d_ff_3_q, d_ff_as_1_nq, d_ff_as_1_q, Manual_out, nand_1_out,
       nand_2_out, nand_3_out, nand_4_out, nor_1_out, nor_2_out, xor_1_out;

  Button #(.activeLow("true")) Auto (.out(Auto_out));
  Button Manual (.out(Manual_out));
  PullUp pullup_1 (.out(Auto_out));
  PullDown pulldown_1 (.out(Manual_out));
  D_FF d_ff_1 (.D(Manual_out), .C(Scan), .Q(d_ff_1_q));  // open: nQ
  nor nor_1 (nor_1_out, d_ff_2_q, d_ff_as_1_nq);
  D_FF d_ff_2 (.D(d_ff_1_q), .C(Scan), .Q(d_ff_2_q));  // open: nQ
  D_FF_AS d_ff_as_1 (.Set(~Auto_out), .D(nor_1_out), .C(nor_2_out), .Clr(~1'b1), .Q(d_ff_as_1_q), .nQ(d_ff_as_1_nq));
  xor xor_1 (xor_1_out, d_ff_1_q, d_ff_2_q);
  nand nand_1 (nand_1_out, Clock, d_ff_as_1_q);
  nand nand_2 (nand_2_out, d_ff_as_1_nq, xor_1_out);
  nand nand_3 (nand_3_out, nand_1_out, nand_2_out);
  nor nor_2 (nor_2_out, Primary, Primary);
  nand nand_4 (nand_4_out, nand_3_out, nand_3_out);
  D_FF d_ff_3 (.D(d_ff_3_nq), .C(nand_4_out), .Q(d_ff_3_q), .nQ(d_ff_3_nq));
  nor nor_3 (Inverted, nand_4_out, d_ff_3_q);
  nor nor_4 (Primary, d_ff_3_nq, nand_4_out);

  // Notes on the sheet:
  //   Clock: Hz: 2
endmodule
